# Fritzing sketch n2k_dashboard (saved by Fritzing 1.0.6)

parts:
  Buck_Converter = RioRand LM2596
  F1_0_2A = FUSE [package=fuse_5mm]
  Adafruit_CAN_Pal_Breakout1 = Adafruit CAN Pal Breakout [part_number=#5708]
  Hoysond_ESP32-S3_2_8"_LCD = IC, DIP package, 8 pins [chip_label="Hoysond ESP32-S3 2.8\" LCD"]

nets:
  N1: Buck_Converter.Pin_1, F1_0_2A.2
  N2K CAN GND: Buck_Converter.Pin_2
  N2: Buck_Converter.Pin_3, Hoysond_ESP32-S3_2_8"_LCD.pin1
  N3: Buck_Converter.Pin_4, Hoysond_ESP32-S3_2_8"_LCD.pin2
  N2K CAN-H: Adafruit_CAN_Pal_Breakout1.CAN_H
  N4: Adafruit_CAN_Pal_Breakout1.CAN1_S, Hoysond_ESP32-S3_2_8"_LCD.pin5
  N5: Adafruit_CAN_Pal_Breakout1.CAN1_TX, Hoysond_ESP32-S3_2_8"_LCD.pin3
  N6: Adafruit_CAN_Pal_Breakout1.CAN1_RX, Hoysond_ESP32-S3_2_8"_LCD.pin4
  N7: Adafruit_CAN_Pal_Breakout1.GND, Hoysond_ESP32-S3_2_8"_LCD.pin7
  N8: Adafruit_CAN_Pal_Breakout1.VCC, Hoysond_ESP32-S3_2_8"_LCD.pin6
  N2K CAN-L: Adafruit_CAN_Pal_Breakout1.CAN_L

notes:
  N2K 12V
  N2K GND
  N2K CAN-H
  N2K CAN-L
  5V

custom parts:
  Adafruit CAN Pal Breakout: If you'd like to connect a board with native CAN Peripheral support, the Adafruit CAN Pal Transceiver will take the 3V logic level signals and convert them to CAN logic levels with the differential signaling required to communicate. Note that not all chips have a CAN peripheral! Some that we know do have it are the ESP32/ESP32-S2/ESP32-S3 (note that ESP32 calls this interface TWAI not CAN)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
